# Fritzing sketch Wiring_OlimexPoeIso_NRF24 (saved by Fritzing 0.9.10b)
breadboards: 1

parts:
  A1 = olimex ESP32-POE-ISO
  NRF24 = NRF24L01+ Breakout Board
  Optional_Display = OLED 0.96" 128x64 I2C SSD1306

nets:
  VCC: A1.Pin_2, A1.Pin_31, NRF24.VCC, Optional_Display.VCC
  GND: A1.Pin_3, A1.Pin_32, NRF24.GND, Optional_Display.GND
  N1: A1.Pin_11, A1.Pin_12
  N2: A1.Pin_17, Optional_Display.SCL
  N3: A1.Pin_18, Optional_Display.SCA
  N4: A1.Pin_23, NRF24.SCK
  N5: A1.Pin_24, NRF24.CS
  N6: A1.Pin_25, NRF24.MISO
  N7: A1.Pin_26, NRF24.MOSI
  N8: A1.Pin_27, NRF24.CE
  N9: A1.Pin_28, NRF24.IRQ

notes:
  Optional Display
  NRF24L01+

custom parts:
  olimex ESP32-POE-ISO: ESP32-PoE is an IoT WIFI/BLE/Ethernet development board with Power-Over-Ethernet feature.
